# Fritzing sketch connections (saved by Fritzing 0.9.3b)

parts:
  LED1 = LEDs [package=led10mm]
  R1 = Resistor [tolerance=±5% resistance=220 package=THT]
  Part2 = HC-SR501 Body Sensor Module
  ESP32-CAM1 = ESP32-CAM

nets:
  N1: LED1.A, Part2.OUT, ESP32-CAM1.GPIO12
  GND: R1.Pin_1, Part2.GND, ESP32-CAM1.GND
  VCC: Part2.VCC, ESP32-CAM1.5V

custom parts:
  HC-SR501 Body Sensor Module: Pyroelectric Infrared PIR Motion Sensor Detector Module
  ESP32-CAM: AIThinker
